// Logisim project 1-Reconhecedor_de_1101_Mealy_Model.circ as structural Verilog: 1 circuit, main circuit main
module main (
  input  clock,
  input  \input ,
  output _1101_found
);

  wire d_ff_1_q, d_ff_2_q, d_ff_2_qn, d_ff_3_q, d_ff_4_q;

  D_Flip_Flop d_ff_1 (.clk(clock), .D(\input ), .Q(d_ff_1_q));  // open: Qn, preset, reset
  D_Flip_Flop d_ff_2 (.clk(clock), .D(d_ff_1_q), .Q(d_ff_2_q), .Qn(d_ff_2_qn));  // open: preset, reset
  D_Flip_Flop d_ff_3 (.clk(clock), .D(d_ff_2_q), .Q(d_ff_3_q));  // open: Qn, preset, reset
  D_Flip_Flop d_ff_4 (.clk(clock), .D(d_ff_3_q), .Q(d_ff_4_q));  // open: Qn, preset, reset
  and and_1 (_1101_found, d_ff_4_q, d_ff_3_q, d_ff_2_qn, d_ff_1_q);

  // Notes on the sheet:
  //   Quando, a partir do último flip-flop mais acima, indo até o último flip-flop mais abaixo, estiver
  //   guardada a sequencia 1101, a saída é 1. Caso contrário é 0.
  //   Reconhecedor da sequência 1101
  //   Funcionamento: a cada clock, o valor de um flip-flop é passado para o outro.
endmodule
