// Logisim project 2-Reconhecedor_de_1101_Moore_Model2.circ as structural Verilog: 2 circuits, main circuit main
module main (
  input  clock,
  input  \input ,
  output _1101_found
);

  wire state_bit0_q, state_bit1_q, state_manager_1_new_state_bit0, state_manager_1_new_state_bit1,
       state_manager_1_new_state_bit2;

  State_Manager state_manager_1 (
    .\input (\input ), .state_bit2(_1101_found), .state_bit1(state_bit1_q), .state_bit0(state_bit0_q),
    .new_state_bit2(state_manager_1_new_state_bit2), .new_state_bit1(state_manager_1_new_state_bit1),
    .new_state_bit0(state_manager_1_new_state_bit0));
  D_Flip_Flop moore_ind__bit2 (
    .clk(clock), .D(state_manager_1_new_state_bit2), .Q(_1101_found));  // open: Qn, preset, reset
  D_Flip_Flop state_bit1 (
    .clk(clock), .D(state_manager_1_new_state_bit1), .Q(state_bit1_q));  // open: Qn, preset, reset
  D_Flip_Flop state_bit0 (
    .clk(clock), .D(state_manager_1_new_state_bit0), .Q(state_bit0_q));  // open: Qn, preset, reset
endmodule

module State_Manager (
  input  \input ,
  input  state_bit2,
  input  state_bit1,
  input  state_bit0,
  output new_state_bit2,
  output new_state_bit1,
  output new_state_bit0
);

  wire and_2_out, and_3_out, and_4_out, and_5_out, and_6_out, not_1_out, not_2_out, not_3_out, not_4_out,
       not_5_out, not_6_out, not_7_out, not_8_out, not_9_out, not_10_out, not_11_out, not_12_out, not_13_out;

  not not_1 (not_1_out, state_bit2);
  not not_2 (not_2_out, state_bit2);
  not not_3 (not_3_out, state_bit0);
  not not_4 (not_4_out, state_bit2);
  not not_5 (not_5_out, state_bit1);
  not not_6 (not_6_out, state_bit1);
  not not_7 (not_7_out, state_bit0);
  not not_8 (not_8_out, \input );
  not not_9 (not_9_out, state_bit2);
  not not_10 (not_10_out, state_bit0);
  not not_11 (not_11_out, state_bit2);
  not not_12 (not_12_out, state_bit1);
  not not_13 (not_13_out, state_bit0);
  and and_1 (new_state_bit2, \input , not_1_out, state_bit1, state_bit0);
  and and_2 (and_2_out, not_2_out, state_bit1, not_3_out);
  or or_1 (new_state_bit1, and_2_out, and_3_out, and_4_out);
  and and_3 (and_3_out, \input , not_4_out, not_5_out, state_bit0);
  and and_4 (and_4_out, \input , state_bit2, not_6_out, not_7_out);
  and and_5 (and_5_out, not_8_out, not_9_out, state_bit1, not_10_out);
  or or_2 (new_state_bit0, and_5_out, and_6_out);
  and and_6 (and_6_out, \input , not_11_out, not_12_out, not_13_out);
endmodule
