// Logisim project 3-Mealy_Moore_Test.circ as structural Verilog: 1 circuit, main circuit main
module main (
  input  in_1,
  output found_by_mealy,
  output found_by_moore
);

  wire clock_1_out;

  Clock clock_1 (.out(clock_1_out));
  _1_Reconhecedor_de_1101_Mealy_Model_main mealy (.clock(clock_1_out), .\input (in_1), ._1101_found(found_by_mealy));
  _2_Reconhecedor_de_1101_Moore_Model2_main moore (.clock(clock_1_out), .\input (in_1), ._1101_found(found_by_moore));
endmodule
