// Logisim project 5-Reconhecedor_de_1010_Moore_Model.circ as structural Verilog: 1 circuit, main circuit main
module main (
  input  \input ,
  output _1010_found
);

  wire clock_1_out, d_ff_1_q, d_ff_2_q, d_ff_2_qn, d_ff_3_q, d_ff_4_q, d_ff_4_qn, d_ff_5_q;

  Clock clock_1 (.out(clock_1_out));
  D_Flip_Flop d_ff_1 (.clk(clock_1_out), .D(\input ), .Q(d_ff_1_q));  // open: Qn, preset, reset
  D_Flip_Flop d_ff_2 (.clk(clock_1_out), .D(d_ff_1_q), .Q(d_ff_2_q), .Qn(d_ff_2_qn));  // open: preset, reset
  D_Flip_Flop d_ff_3 (.clk(clock_1_out), .D(d_ff_2_q), .Q(d_ff_3_q));  // open: Qn, preset, reset
  D_Flip_Flop d_ff_4 (.clk(clock_1_out), .D(d_ff_3_q), .Q(d_ff_4_q), .Qn(d_ff_4_qn));  // open: preset, reset
  D_Flip_Flop d_ff_5 (.clk(clock_1_out), .D(d_ff_4_q), .Q(d_ff_5_q));  // open: Qn, preset, reset
  and and_1 (_1010_found, d_ff_5_q, d_ff_4_qn, d_ff_3_q, d_ff_2_qn);

  // Notes on the sheet:
  //   Funcionamento: a cada clock, o valor de um flip-flop é passado para o outro.
  //   Quando, a partir do último flip-flop mais acima, indo até o penúltimo flip-flop mais abaixo
  //   estiver guardada a sequencia 1010, a saída é 1. Caso contrário é 0.
  //   Reconhecedor da sequência 1010
endmodule
