// Logisim project 6-Reconhecedor_de_101_Mealy_Model.circ as structural Verilog: 2 circuits, main circuit main
module main (
  input  \input ,
  output _101_found
);

  wire and_1_out, clock_1_out, state_bit0_q, state_bit0_qn, state_bit1_q, state_manager_1_new_state_bit0,
       state_manager_1_new_state_bit1;

  Clock clock_1 (.out(clock_1_out));
  State_Manager state_manager_1 (
    .\input (\input ), .state_bit1(state_bit1_q), .state_bit0(state_bit0_q),
    .new_state_bit1(state_manager_1_new_state_bit1), .new_state_bit0(state_manager_1_new_state_bit0));
  D_Flip_Flop state_bit1 (
    .clk(clock_1_out), .D(state_manager_1_new_state_bit1), .Q(state_bit1_q));  // open: Qn, preset, reset
  D_Flip_Flop state_bit0 (
    .clk(clock_1_out), .D(state_manager_1_new_state_bit0), .Q(state_bit0_q), .Qn(state_bit0_qn));  // open: preset, reset
  and and_1 (and_1_out, \input , state_bit1_q, state_bit0_qn);
  or or_1 (_101_found, _101_found, and_1_out);
endmodule

module State_Manager (
  input  \input ,
  input  state_bit1,
  input  state_bit0,
  output new_state_bit1,
  output new_state_bit0
);

  wire not_1_out, not_2_out, not_3_out;

  not not_1 (not_1_out, \input );
  not not_2 (not_2_out, state_bit1);
  not not_3 (not_3_out, state_bit1);
  and and_1 (new_state_bit1, not_1_out, not_2_out, state_bit0);
  and and_2 (new_state_bit0, \input , not_3_out);
endmodule
