// Logisim project 7-Reconhecedor_de_x111_Mealy_Model.circ as structural Verilog: 1 circuit, main circuit main
module main (
  input  \input ,
  output x111_found
);

  wire clock_1_out, d_ff_1_q, d_ff_2_q, d_ff_3_q, d_ff_4_q;

  Clock clock_1 (.out(clock_1_out));
  D_Flip_Flop d_ff_1 (.clk(clock_1_out), .D(\input ), .Q(d_ff_1_q));  // open: Qn, preset, reset
  D_Flip_Flop d_ff_2 (.clk(clock_1_out), .D(d_ff_1_q), .Q(d_ff_2_q));  // open: Qn, preset, reset
  D_Flip_Flop d_ff_3 (.clk(clock_1_out), .D(d_ff_2_q), .Q(d_ff_3_q));  // open: Qn, preset, reset
  D_Flip_Flop d_ff_4 (.clk(clock_1_out), .D(d_ff_3_q), .Q(d_ff_4_q));  // open: Qn, preset, reset
  and and_1 (x111_found, d_ff_4_q, d_ff_3_q, d_ff_2_q);

  // Notes on the sheet:
  //   Quando, a partir do último flip-flop mais acima, indo até o penúltimo flip-flop mais abaixo,
  //   estiver guardada a sequencia 111, a saída é 1. Caso contrário é 0.
  //   Reconhecedor da sequência x111
  //   Funcionamento: a cada clock, o valor de um flip-flop é passado para o outro.
endmodule
