// Logisim project 8-Reconhecedor_de_111_ou_000_Mealy_Model.circ as structural Verilog: 1 circuit, main circuit main
module main (
  input  \input ,
  output _111_or_000_found
);

  wire and_1_out, and_2_out, clock_1_out, d_ff_1_q, d_ff_1_qn, d_ff_2_q, d_ff_2_qn, d_ff_3_q, d_ff_3_qn;

  Clock clock_1 (.out(clock_1_out));
  D_Flip_Flop d_ff_1 (.clk(clock_1_out), .D(\input ), .Q(d_ff_1_q), .Qn(d_ff_1_qn));  // open: preset, reset
  D_Flip_Flop d_ff_2 (.clk(clock_1_out), .D(d_ff_1_q), .Q(d_ff_2_q), .Qn(d_ff_2_qn));  // open: preset, reset
  D_Flip_Flop d_ff_3 (.clk(clock_1_out), .D(d_ff_2_q), .Q(d_ff_3_q), .Qn(d_ff_3_qn));  // open: preset, reset
  and and_1 (and_1_out, d_ff_3_q, d_ff_2_q, d_ff_1_q);
  and and_2 (and_2_out, d_ff_3_qn, d_ff_2_qn, d_ff_1_qn);
  or or_1 (_111_or_000_found, and_1_out, and_2_out);

  // Notes on the sheet:
  //   Quando, a partir do último flip-flop mais acima, indo até o último flip-flop mais abaixo,
  //   estiver guardada a sequencia 111 ou 000, a saída é 1. Caso contrário é 0.
  //   Reconhecedor da sequência 111 ou 000
  //   Funcionamento: a cada clock, o valor de um flip-flop é passado para o outro.
endmodule
