// Logisim project Flip-Flop-D.circ as structural Verilog: 1 circuit, main circuit main
module main (
  input  \input ,
  output last_saved_input,
  output nlast_saved_input
);

  wire clock_1_out, nand_1_out, nand_2_out, not_1_out;

  not not_1 (not_1_out, \input );
  Clock clock_1 (.out(clock_1_out));
  nand nand_1 (nand_1_out, \input , clock_1_out);
  nand nand_2 (nand_2_out, not_1_out, clock_1_out);
  nand nand_3 (last_saved_input, nand_1_out, nlast_saved_input);
  nand nand_4 (nlast_saved_input, last_saved_input, nand_2_out);
endmodule
