// Logisim project 2-RAM_1X4_with_2_1X2_RAMs.circ as structural Verilog: 1 circuit, main circuit main
module main (
  input  enable,
  input  read___write,
  input  clock,
  input  [3:0] data,
  input  clear,
  output [3:0] last_saved_data_or_0000
);

  RAM_1X2_main bit3_2 (
    .enable(enable), .read___write(read___write), .clock(clock), .data(data[3:2]), .clear(clear),
    .last_saved_data_or_00(last_saved_data_or_0000[3:2]));
  RAM_1X2_main bit1_0 (
    .enable(enable), .read___write(read___write), .clock(clock), .data(data[1:0]), .clear(clear),
    .last_saved_data_or_00(last_saved_data_or_0000[1:0]));
endmodule
