// Logisim project 3-RAM_2X8.circ as structural Verilog: 1 circuit, main circuit main
module main (
  input  address,
  input  read___write,
  input  clock,
  input  [7:0] data,
  input  clear,
  output [7:0] mem_saved_data_or_00000000
);

  wire demultiplexer_1_out0, demultiplexer_1_out1;
  wire [7:0] address_0_last_saved_data_or_00000000, address_1_last_saved_data_or_00000000;

  Demultiplexer #(.enable("false")) demultiplexer_1 (
    .out0(demultiplexer_1_out0), .out1(demultiplexer_1_out1), .in(1'b1), .sel(address));
  RAM_1X8_main address_0 (
    .enable(demultiplexer_1_out0), .read___write(read___write), .clock(clock), .data(data), .clear(clear),
    .last_saved_data_or_00000000(address_0_last_saved_data_or_00000000));
  RAM_1X8_main address_1 (
    .enable(demultiplexer_1_out1), .read___write(read___write), .clock(clock), .data(data), .clear(clear),
    .last_saved_data_or_00000000(address_1_last_saved_data_or_00000000));
  Multiplexer #(.width(8), .enable("false")) multiplexer_1 (
    .in0(address_0_last_saved_data_or_00000000), .in1(address_1_last_saved_data_or_00000000),
    .out(mem_saved_data_or_00000000), .sel(address));
endmodule
