// Logisim project 4-RAM_4X8.circ as structural Verilog: 1 circuit, main circuit main
module main (
  input  [1:0] address,
  input  read___write,
  input  clock,
  input  [7:0] data,
  input  clear,
  output [7:0] mem_saved_data_or_00000000
);

  wire demultiplexer_1_out0, demultiplexer_1_out1, demultiplexer_1_out2, demultiplexer_1_out3;
  wire [7:0] address_0_last_saved_data_or_00000000, address_1_last_saved_data_or_00000000,
       address_2_last_saved_data_or_00000000, address_3_last_saved_data_or_00000000;

  Demultiplexer #(.select(2), .enable("false")) demultiplexer_1 (
    .out0(demultiplexer_1_out0), .out1(demultiplexer_1_out1), .out2(demultiplexer_1_out2),
    .out3(demultiplexer_1_out3), .in(1'b1), .sel(address));
  RAM_1X8_main address_0 (
    .enable(demultiplexer_1_out0), .read___write(read___write), .clock(clock), .data(data), .clear(clear),
    .last_saved_data_or_00000000(address_0_last_saved_data_or_00000000));
  RAM_1X8_main address_1 (
    .enable(demultiplexer_1_out1), .read___write(read___write), .clock(clock), .data(data), .clear(clear),
    .last_saved_data_or_00000000(address_1_last_saved_data_or_00000000));
  RAM_1X8_main address_2 (
    .enable(demultiplexer_1_out2), .read___write(read___write), .clock(clock), .data(data), .clear(clear),
    .last_saved_data_or_00000000(address_2_last_saved_data_or_00000000));
  RAM_1X8_main address_3 (
    .enable(demultiplexer_1_out3), .read___write(read___write), .clock(clock), .data(data), .clear(clear),
    .last_saved_data_or_00000000(address_3_last_saved_data_or_00000000));
  Multiplexer #(.select(2), .width(8), .enable("false")) multiplexer_1 (
    .in0(address_0_last_saved_data_or_00000000), .in1(address_1_last_saved_data_or_00000000),
    .in2(address_2_last_saved_data_or_00000000), .in3(address_3_last_saved_data_or_00000000),
    .out(mem_saved_data_or_00000000), .sel(address));
endmodule
