// Logisim project 5-RAM_8X8.circ as structural Verilog: 1 circuit, main circuit main
module main (
  input  [2:0] address,
  input  read___write,
  input  clock,
  input  [7:0] data,
  input  clear,
  output [7:0] mem_saved_data_or_00000000
);

  wire demultiplexer_2_out0, demultiplexer_2_out1;
  wire [1:0] demultiplexer_1_out0, demultiplexer_1_out1;
  wire [7:0] main_1_mem_saved_data_or_00000000, main_2_mem_saved_data_or_00000000;

  Demultiplexer #(.width(2), .enable("false")) demultiplexer_1 (
    .out0(demultiplexer_1_out0), .out1(demultiplexer_1_out1), .in(address[1:0]), .sel(address[2]));
  Demultiplexer #(.enable("false")) demultiplexer_2 (
    .out0(demultiplexer_2_out0), .out1(demultiplexer_2_out1), .in(clock), .sel(address[2]));
  _4_RAM_4X8_main main_1 (
    .address(demultiplexer_1_out0), .read___write(read___write), .clock(demultiplexer_2_out0), .data(data),
    .clear(clear), .mem_saved_data_or_00000000(main_1_mem_saved_data_or_00000000));
  _4_RAM_4X8_main main_2 (
    .address(demultiplexer_1_out1), .read___write(read___write), .clock(demultiplexer_2_out1), .data(data),
    .clear(clear), .mem_saved_data_or_00000000(main_2_mem_saved_data_or_00000000));
  Multiplexer #(.width(8), .enable("false")) multiplexer_1 (
    .in0(main_1_mem_saved_data_or_00000000), .in1(main_2_mem_saved_data_or_00000000),
    .out(mem_saved_data_or_00000000), .sel(address[2]));
endmodule
