// Logisim project 6-RAM_1X16.circ as structural Verilog: 1 circuit, main circuit main
module main (
  input  enable,
  input  read___write,
  input  clock,
  input  [15:0] data,
  input  clear,
  output [15:0] last_saved_data_or_0000000000000000
);

  RAM_1X8_main bit15_8 (
    .enable(enable), .read___write(read___write), .clock(clock), .data(data[15:8]), .clear(clear),
    .last_saved_data_or_00000000(last_saved_data_or_0000000000000000[15:8]));
  RAM_1X8_main bit7_0 (
    .enable(enable), .read___write(read___write), .clock(clock), .data(data[7:0]), .clear(clear),
    .last_saved_data_or_00000000(last_saved_data_or_0000000000000000[7:0]));
endmodule
