// Logisim project RAM_1X1.circ as structural Verilog: 1 circuit, main circuit main
module main (
  input  enable,
  input  read___write,
  input  clock,
  input  data,
  input  clear,
  output last_saved_data_or_0
);

  wire and_1_out, and_2_out, jk_master_slave_last_saved_data, not_1_out, not_2_out;

  not not_1 (not_1_out, read___write);
  and and_1 (and_1_out, enable, read___write, clock);
  Flip_Flop_JK_Master_Slave_main jk_master_slave (
    .clock(and_1_out), .J(data), .K(not_2_out), .preset(1'b0), .clear(clear),
    .last_saved_data(jk_master_slave_last_saved_data));  // open: nlast_saved_data
  not not_2 (not_2_out, data);
  and and_2 (and_2_out, not_1_out, clock);
  and and_3 (last_saved_data_or_0, enable, and_2_out, jk_master_slave_last_saved_data);
endmodule
