// Logisim project RAM_1X2.circ as structural Verilog: 1 circuit, main circuit main
module main (
  input  enable,
  input  read___write,
  input  clock,
  input  [1:0] data,
  input  clear,
  output [1:0] last_saved_data_or_00
);

  RAM_1X1_main bit1 (
    .enable(enable), .read___write(read___write), .clock(clock), .data(data[1]), .clear(clear),
    .last_saved_data_or_0(last_saved_data_or_00[1]));
  RAM_1X1_main bit0 (
    .enable(enable), .read___write(read___write), .clock(clock), .data(data[0]), .clear(clear),
    .last_saved_data_or_0(last_saved_data_or_00[0]));
endmodule
