// Logisim project 2-Shift_Left_Register_all_bits_load.circ as structural Verilog: 1 circuit, main circuit main
module main (
  input  clock,
  input  data,
  input  load,
  input  clear,
  input  bit0,
  input  bit1,
  input  bit2,
  input  bit3,
  input  bit4
);

  wire main_1_saved_data, main_2_saved_data, main_3_saved_data, main_4_saved_data, main_5_saved_data;

  // Probe on main_5_saved_data
  // Probe on main_4_saved_data
  Flip_Flop_D_with_triggered_bit_load_main main_1 (
    .clock(clock), .data(data), .load(load), .bit_to_load(bit0), .preset(1'b0), .clear(clear),
    .saved_data(main_1_saved_data));  // open: nsaved_data
  // Probe on main_3_saved_data
  Flip_Flop_D_with_triggered_bit_load_main main_2 (
    .clock(clock), .data(main_1_saved_data), .load(load), .bit_to_load(bit1), .preset(1'b0), .clear(clear),
    .saved_data(main_2_saved_data));  // open: nsaved_data
  Flip_Flop_D_with_triggered_bit_load_main main_3 (
    .clock(clock), .data(main_2_saved_data), .load(load), .bit_to_load(bit2), .preset(1'b0), .clear(clear),
    .saved_data(main_3_saved_data));  // open: nsaved_data
  // Probe on main_2_saved_data
  Flip_Flop_D_with_triggered_bit_load_main main_4 (
    .clock(clock), .data(main_3_saved_data), .load(load), .bit_to_load(bit3), .preset(1'b0), .clear(clear),
    .saved_data(main_4_saved_data));  // open: nsaved_data
  // Probe on main_1_saved_data
  Flip_Flop_D_with_triggered_bit_load_main main_5 (
    .clock(clock), .data(main_4_saved_data), .load(load), .bit_to_load(bit4), .preset(1'b0), .clear(clear),
    .saved_data(main_5_saved_data));  // open: nsaved_data
endmodule
