// Logisim project 4-Negated_Circular_Shift_Left_Register_1bit_load.circ as structural Verilog: 1 circuit, main circuit main
module main (
  input  clock,
  input  data,
  input  load,
  input  bit_to_load,
  input  clear
);

  wire main_1_saved_data, main_2_saved_data, main_3_saved_data, main_4_saved_data, main_5_nsaved_data,
       main_5_saved_data, or_1_out;

  // Probe on main_5_saved_data
  or or_1 (or_1_out, main_5_nsaved_data, data);
  // Probe on main_4_saved_data
  Flip_Flop_D_with_triggered_bit_load_main main_1 (
    .clock(clock), .data(or_1_out), .load(load), .bit_to_load(bit_to_load), .preset(1'b0), .clear(clear),
    .saved_data(main_1_saved_data));  // open: nsaved_data
  // Probe on main_3_saved_data
  Flip_Flop_D_with_triggered_bit_load_main main_2 (
    .clock(clock), .data(main_1_saved_data), .load(1'b0), .preset(1'b0), .clear(clear),
    .saved_data(main_2_saved_data));  // open: bit_to_load, nsaved_data
  Flip_Flop_D_with_triggered_bit_load_main main_3 (
    .clock(clock), .data(main_2_saved_data), .load(1'b0), .preset(1'b0), .clear(clear),
    .saved_data(main_3_saved_data));  // open: bit_to_load, nsaved_data
  // Probe on main_2_saved_data
  Flip_Flop_D_with_triggered_bit_load_main main_4 (
    .clock(clock), .data(main_3_saved_data), .load(1'b0), .preset(1'b0), .clear(clear),
    .saved_data(main_4_saved_data));  // open: bit_to_load, nsaved_data
  // Probe on main_1_saved_data
  Flip_Flop_D_with_triggered_bit_load_main main_5 (
    .clock(clock), .data(main_4_saved_data), .load(1'b0), .preset(1'b0), .clear(clear),
    .saved_data(main_5_saved_data), .nsaved_data(main_5_nsaved_data));  // open: bit_to_load
endmodule
