// Logisim project Flip_Flop_D_with_triggered_bit_load.circ as structural Verilog: 1 circuit, main circuit main
module main (
  input  preset,
  input  clock,
  input  data,
  input  load,
  input  bit_to_load,
  input  clear,
  output saved_data,
  output nsaved_data
);

  wire and_1_out, and_2_out, not_1_out, not_2_out, or_1_out, or_2_out;

  not not_1 (not_1_out, data);
  and and_1 (and_1_out, load, bit_to_load);
  or or_1 (or_1_out, and_1_out, preset);
  or or_2 (or_2_out, and_2_out, clear);
  and and_2 (and_2_out, load, not_2_out);
  not not_2 (not_2_out, bit_to_load);
  Flip_Flop_JK_Master_Slave_main main_1 (
    .clock(clock), .J(data), .K(not_1_out), .preset(or_1_out), .clear(or_2_out),
    .last_saved_data(saved_data), .nlast_saved_data(nsaved_data));
endmodule
