// Logisim project Flip_Flop_JK_Master_Slave.circ as structural Verilog: 1 circuit, main circuit main
module main (
  input  clock,
  input  preset,
  input  J,
  input  K,
  input  clear,
  output last_saved_data,
  output nlast_saved_data
);

  wire and_1_out, and_2_out, main_1_last_saved_data, main_1_nlast_saved_data, not_1_out;

  not not_1 (not_1_out, clock);
  and and_1 (and_1_out, nlast_saved_data, J);
  and and_2 (and_2_out, last_saved_data, K);
  Flip_Flop_SR_main main_1 (
    .set(and_1_out), .clock(clock), .reset(and_2_out), .preset(preset), .clear(clear),
    .last_saved_data(main_1_last_saved_data), .nlast_saved_data(main_1_nlast_saved_data));
  Flip_Flop_SR_main main_2 (
    .set(main_1_last_saved_data), .clock(not_1_out), .reset(main_1_nlast_saved_data), .preset(preset),
    .clear(clear), .last_saved_data(last_saved_data), .nlast_saved_data(nlast_saved_data));
endmodule
