// Logisim project 3-decade_crescent_asynchronous_counter.circ as structural Verilog: 1 circuit, main circuit main
module main (
  input  clock,
  input  clear,
  input  load,
  output [4:0] out_4
);

  wire [7:5] main_1_current_value;

  programmable_counter_main main_1 (
    .clock(clock), .clear(clear), .load(load), .current_value({main_1_current_value, out_4}),
    .lower_limit({8{1'b0}}), .upper_limit(8'h9), .crescent_decrescent(1'b0));

  // Notes on the sheet:
  //   USAGE: clear, input lower limit, input upper limit, load (2x), clock
endmodule
