// Logisim project 1-RAM_1X4.circ as structural Verilog: 1 circuit, main circuit main
module main (
  input  enable,
  input  read___write,
  input  clock,
  input  [3:0] data,
  input  clear,
  output [3:0] last_saved_data_or_0000
);

  RAM_1X1_main bit3 (
    .enable(enable), .read___write(read___write), .clock(clock), .data(data[3]), .clear(clear),
    .last_saved_data_or_0(last_saved_data_or_0000[3]));
  RAM_1X1_main bit2 (
    .enable(enable), .read___write(read___write), .clock(clock), .data(data[2]), .clear(clear),
    .last_saved_data_or_0(last_saved_data_or_0000[2]));
  RAM_1X1_main bit1 (
    .enable(enable), .read___write(read___write), .clock(clock), .data(data[1]), .clear(clear),
    .last_saved_data_or_0(last_saved_data_or_0000[1]));
  RAM_1X1_main bit0 (
    .enable(enable), .read___write(read___write), .clock(clock), .data(data[0]), .clear(clear),
    .last_saved_data_or_0(last_saved_data_or_0000[0]));
endmodule
