// Logisim project RAM_1X1.circ as structural Verilog: 1 circuit, main circuit main
module main (
  input  enable,
  input  read___write,
  input  clock,
  input  data,
  input  clear,
  output last_saved_data_or_0
);

  wire and_1_out, jk_master_slave_last_saved_data, not_1_out;

  Flip_Flop_JK_Master_Slave_main jk_master_slave (
    .clock(and_1_out), .J(data), .K(not_1_out), .preset(1'b0), .clear(clear),
    .last_saved_data(jk_master_slave_last_saved_data));  // open: nlast_saved_data
  and and_1 (and_1_out, enable, read___write, clock);
  not not_1 (not_1_out, data);
  and and_2 (last_saved_data_or_0, enable, jk_master_slave_last_saved_data);
endmodule
