// Logisim project RAM_1X8.circ as structural Verilog: 1 circuit, main circuit main
module main (
  input  enable,
  input  read___write,
  input  clock,
  input  [7:0] data,
  input  clear,
  output [7:0] last_saved_data_or_00000000
);

  _1_RAM_1X4_main bit7_4 (
    .enable(enable), .read___write(read___write), .clock(clock), .data(data[7:4]), .clear(clear),
    .last_saved_data_or_0000(last_saved_data_or_00000000[7:4]));
  _1_RAM_1X4_main bit3_0 (
    .enable(enable), .read___write(read___write), .clock(clock), .data(data[3:0]), .clear(clear),
    .last_saved_data_or_0000(last_saved_data_or_00000000[3:0]));
endmodule
