// Logisim project Somador_Algebrico_8bits.circ as structural Verilog: 1 circuit, main circuit main
module main (
  input  [7:0] num1,
  input  [7:0] num2,
  input  somar_sub,
  output [7:0] num1_____num2,
  output b___a__just_subtraction,
  output b____a__just_subtraction
);

  wire main_1_send_bit;
  wire [7:0] multiplexer_1_out, not_1_out;

  assign not_1_out = ~num2;  // NOT_Gate not_1, 8 bits wide
  Multiplexer #(.width(8), .enable("false")) multiplexer_1 (
    .in0(num2), .in1(not_1_out), .out(multiplexer_1_out), .sel(somar_sub));
  Somador_completo_8bits_main main_1 (
    .a(num1), .b(multiplexer_1_out), .received_bit(somar_sub), .a___b(num1_____num2),
    .send_bit(main_1_send_bit));
  not not_2 (b___a__just_subtraction, main_1_send_bit);
  nor nor_1 (b____a__just_subtraction, num1_____num2[7], num1_____num2[6], num1_____num2[5], num1_____num2[4], num1_____num2[3], num1_____num2[2], num1_____num2[1], num1_____num2[0]);
endmodule
