// Logisim project Somador_completo_8bits.circ as structural Verilog: 1 circuit, main circuit main
module main (
  input  [7:0] a,
  input  [7:0] b,
  input  received_bit,
  output [7:0] a___b,
  output send_bit
);

  wire main_1_p4, main_2_p4, main_3_p4, main_4_p4, main_5_p4, main_6_p4, main_7_p4;

  // Somador_completo_a_mais_b_mais_bit_recebido_main main_1: pin names not known; wires that end beside it: a[0], b[0], received_bit, main_1_p4, a___b[0]
  // Somador_completo_a_mais_b_mais_bit_recebido_main main_2: pin names not known; wires that end beside it: a[1], b[1], main_1_p4, main_2_p4, a___b[1]
  // Somador_completo_a_mais_b_mais_bit_recebido_main main_3: pin names not known; wires that end beside it: a[2], b[2], main_2_p4, main_3_p4, a___b[2]
  // Somador_completo_a_mais_b_mais_bit_recebido_main main_4: pin names not known; wires that end beside it: a[3], b[3], main_3_p4, main_4_p4, a___b[3]
  // Somador_completo_a_mais_b_mais_bit_recebido_main main_5: pin names not known; wires that end beside it: a[4], b[4], main_4_p4, main_5_p4, a___b[4]
  // Somador_completo_a_mais_b_mais_bit_recebido_main main_6: pin names not known; wires that end beside it: a[5], b[5], main_5_p4, main_6_p4, a___b[5]
  // Somador_completo_a_mais_b_mais_bit_recebido_main main_7: pin names not known; wires that end beside it: a[6], b[6], main_6_p4, main_7_p4, a___b[6]
  // Somador_completo_a_mais_b_mais_bit_recebido_main main_8: pin names not known; wires that end beside it: a[7], b[7], main_7_p4, send_bit, a___b[7]
endmodule
