// Logisim project programmable_counter.circ as structural Verilog: 1 circuit, main circuit main
module main (
  input  clock,
  input  clear,
  input  load,
  input  [7:0] lower_limit,
  input  [7:0] upper_limit,
  input  crescent_decrescent,
  output [7:0] current_value
);

  wire and_1_out, main_5_last_saved_data, not_1_out, or_1_out,
       upper_limit___current_value_b____a__just_subtraction;
  wire [7:0] lower_limit___upper_limit___current_value_num1_____num2,
       lower_limit_last_saved_data_or_00000000, main_1_saved_data, upper_limit___current_value_num1_____num2,
       upper_limit_last_saved_data_or_00000000;

  not not_1 (not_1_out, clock);
  and and_1 (and_1_out, main_5_last_saved_data, not_1_out);
  or or_1 (or_1_out, and_1_out, load);
  Multiplexer #(.width(8), .enable("false")) multiplexer_1 (
    .in0(main_1_saved_data), .in1(lower_limit___upper_limit___current_value_num1_____num2),
    .out(current_value), .sel(crescent_decrescent));
  Flip_Flop_JK_with_triggered_bit_load_main main_1 (
    .clock(clock), .J(1'b1), .K(1'b1), .load(or_1_out),
    .bit_to_load(lower_limit_last_saved_data_or_00000000[0]), .preset(1'b0), .clear(clear),
    .saved_data(main_1_saved_data[0]));  // open: nsaved_data
  RAM_1X8_main u_lower_limit (
    .enable(1'b1), .read___write(or_1_out), .clock(1'b1), .data(lower_limit), .clear(clear),
    .last_saved_data_or_00000000(lower_limit_last_saved_data_or_00000000));
  Flip_Flop_JK_with_triggered_bit_load_main main_2 (
    .clock(main_1_saved_data[0]), .J(1'b1), .K(1'b1), .load(or_1_out),
    .bit_to_load(lower_limit_last_saved_data_or_00000000[1]), .preset(1'b0), .clear(clear),
    .saved_data(main_1_saved_data[1]));  // open: nsaved_data
  RAM_1X8_main u_upper_limit (
    .enable(1'b1), .read___write(or_1_out), .clock(1'b1), .data(upper_limit), .clear(clear),
    .last_saved_data_or_00000000(upper_limit_last_saved_data_or_00000000));
  Somador_Algebrico_8bits_main lower_limit___upper_limit___current_value (
    .num1(lower_limit_last_saved_data_or_00000000), .num2(upper_limit___current_value_num1_____num2),
    .somar_sub(1'b0), .num1_____num2(lower_limit___upper_limit___current_value_num1_____num2));  // open: b___a__just_subtraction, b____a__just_subtraction
  Flip_Flop_JK_with_triggered_bit_load_main main_3 (
    .clock(main_1_saved_data[1]), .J(1'b1), .K(1'b1), .load(or_1_out),
    .bit_to_load(lower_limit_last_saved_data_or_00000000[2]), .preset(1'b0), .clear(clear),
    .saved_data(main_1_saved_data[2]));  // open: nsaved_data
  Somador_Algebrico_8bits_main upper_limit___current_value (
    .num1(upper_limit_last_saved_data_or_00000000), .num2(main_1_saved_data), .somar_sub(1'b1),
    .num1_____num2(upper_limit___current_value_num1_____num2),
    .b____a__just_subtraction(upper_limit___current_value_b____a__just_subtraction));  // open: b___a__just_subtraction
  Flip_Flop_JK_with_triggered_bit_load_main main_4 (
    .clock(main_1_saved_data[2]), .J(1'b1), .K(1'b1), .load(or_1_out),
    .bit_to_load(lower_limit_last_saved_data_or_00000000[3]), .preset(1'b0), .clear(clear),
    .saved_data(main_1_saved_data[3]));  // open: nsaved_data
  Flip_Flop_D_main main_5 (
    .data(upper_limit___current_value_b____a__just_subtraction), .clock(clock), .preset(1'b0), .clear(clear),
    .last_saved_data(main_5_last_saved_data));  // open: nlast_saved_data
  Flip_Flop_JK_with_triggered_bit_load_main main_6 (
    .clock(main_1_saved_data[3]), .J(1'b1), .K(1'b1), .load(or_1_out),
    .bit_to_load(lower_limit_last_saved_data_or_00000000[4]), .preset(1'b0), .clear(clear),
    .saved_data(main_1_saved_data[4]));  // open: nsaved_data
  Flip_Flop_JK_with_triggered_bit_load_main main_7 (
    .clock(main_1_saved_data[4]), .J(1'b1), .K(1'b1), .load(or_1_out),
    .bit_to_load(lower_limit_last_saved_data_or_00000000[5]), .preset(1'b0), .clear(clear),
    .saved_data(main_1_saved_data[5]));  // open: nsaved_data
  Flip_Flop_JK_with_triggered_bit_load_main main_8 (
    .clock(main_1_saved_data[5]), .J(1'b1), .K(1'b1), .load(or_1_out),
    .bit_to_load(lower_limit_last_saved_data_or_00000000[6]), .preset(1'b0), .clear(clear),
    .saved_data(main_1_saved_data[6]));  // open: nsaved_data
  Flip_Flop_JK_with_triggered_bit_load_main main_9 (
    .clock(main_1_saved_data[6]), .J(1'b1), .K(1'b1), .load(or_1_out),
    .bit_to_load(lower_limit_last_saved_data_or_00000000[7]), .preset(1'b0), .clear(clear),
    .saved_data(main_1_saved_data[7]));  // open: nsaved_data

  // Notes on the sheet:
  //   USAGE: clear, input lower limit, input upper limit, load (2x), clock
endmodule
