// Logisim project 1-Porta_OR_usando_NAND.circ as structural Verilog: 1 circuit, main circuit main
module main (
  input  p,
  input  q,
  output out_3
);

  wire nand_1_out, nand_2_out;

  nand nand_1 (nand_1_out, p, p);
  nand nand_2 (nand_2_out, q, q);
  nand nand_3 (out_3, nand_1_out, nand_2_out);

  // Notes on the sheet:
  //   (p OR q) using NAND
  //   NOT using NAND
  //   NOT using NAND
endmodule
