// Logisim project 2-Porta_AND_usando_NOR.circ as structural Verilog: 1 circuit, main circuit main
module main (
  input  p,
  input  q,
  output out_3
);

  wire nor_1_out, nor_2_out;

  nor nor_1 (nor_1_out, p, p);
  nor nor_2 (nor_2_out, q, q);
  nor nor_3 (out_3, nor_1_out, nor_2_out);

  // Notes on the sheet:
  //   (p AND q) using NOR
  //   NOT using NOR
  //   NOT using NOR
endmodule
