// Logisim project 3-Porta_AND_usando_NAND.circ as structural Verilog: 1 circuit, main circuit main
module main (
  input  p,
  input  q,
  output out_3
);

  wire nand_1_out;

  nand nand_1 (nand_1_out, p, q);
  nand nand_2 (out_3, nand_1_out, nand_1_out);

  // Notes on the sheet:
  //   (p AND q) using NAND
  //   NOT using NAND
endmodule
