// Logisim project 4-Porta_OR_usando_NOR.circ as structural Verilog: 1 circuit, main circuit main
module main (
  input  p,
  input  q,
  output out_3
);

  wire nor_2_out;

  nor nor_1 (out_3, nor_2_out, nor_2_out);
  nor nor_2 (nor_2_out, p, q);

  // Notes on the sheet:
  //   (p OR q) using NOR
  //   NOT using NOR
endmodule
