// Logisim project 5-Porta_XOR_usando_NAND.circ as structural Verilog: 1 circuit, main circuit main
module main (
  input  p,
  input  q,
  output out_3
);

  wire nand_1_out, nand_2_out, nand_3_out, nand_4_out, nand_5_out, nand_6_out, nand_7_out, nand_8_out,
       nand_9_out;

  nand nand_1 (nand_1_out, p, p);
  nand nand_2 (nand_2_out, q, q);
  nand nand_3 (nand_3_out, nand_1_out, nand_1_out);
  nand nand_4 (nand_4_out, nand_2_out, nand_2_out);
  nand nand_5 (nand_5_out, p, p);
  nand nand_6 (nand_6_out, q, q);
  nand nand_7 (nand_7_out, nand_3_out, nand_4_out);
  nand nand_8 (nand_8_out, nand_7_out, nand_9_out);
  nand nand_9 (nand_9_out, nand_5_out, nand_6_out);
  nand nand_10 (out_3, nand_8_out, nand_8_out);

  // Notes on the sheet:
  //   NOT using NAND
  //   NOT using NAND
  //   (p XOR q) using NAND
  //   OR using NAND
  //   OR using NAND
  //   AND using NAND
endmodule
