// Logisim project 6-Porta_XNOR_usando_NOR.circ as structural Verilog: 1 circuit, main circuit main
module main (
  input  p,
  input  q,
  output out_3
);

  wire nor_1_out, nor_2_out, nor_3_out, nor_4_out, nor_5_out, nor_6_out, nor_7_out, nor_8_out, nor_9_out;

  nor nor_1 (nor_1_out, p, p);
  nor nor_2 (nor_2_out, q, q);
  nor nor_3 (nor_3_out, nor_1_out, nor_1_out);
  nor nor_4 (nor_4_out, nor_2_out, nor_2_out);
  nor nor_5 (nor_5_out, p, p);
  nor nor_6 (nor_6_out, q, q);
  nor nor_7 (nor_7_out, nor_3_out, nor_4_out);
  nor nor_8 (nor_8_out, nor_7_out, nor_9_out);
  nor nor_9 (nor_9_out, nor_5_out, nor_6_out);
  nor nor_10 (out_3, nor_8_out, nor_8_out);

  // Notes on the sheet:
  //   NOT using NOR
  //   NOT using NOR
  //   (p XNOR q) using NOR
  //   AND using NOR
  //   AND using NOR
  //   OR using NOR
endmodule
