// Logisim project Extra1-Porta_p_AND_~q_usando_NOR.circ as structural Verilog: 1 circuit, main circuit main
module main (
  input  p,
  input  q,
  output out_3
);

  wire nor_1_out, nor_2_out, nor_3_out;

  nor nor_1 (nor_1_out, q, q);
  nor nor_2 (nor_2_out, p, p);
  nor nor_3 (nor_3_out, nor_1_out, nor_1_out);
  nor nor_4 (out_3, nor_2_out, nor_3_out);

  // Notes on the sheet:
  //   NOT using NOR
  //   (p AND ~q) using NOR
  //   AND using NOR
endmodule
