// Logisim project Extra2-Porta_p_AND_~q_usando_NAND.circ as structural Verilog: 1 circuit, main circuit main
module main (
  input  p,
  input  q,
  output out_3
);

  wire nand_1_out, nand_2_out;

  nand nand_1 (nand_1_out, q, q);
  nand nand_2 (nand_2_out, p, nand_1_out);
  nand nand_3 (out_3, nand_2_out, nand_2_out);

  // Notes on the sheet:
  //   NOT using NAND
  //   (p AND ~q) using NAND
  //   AND using NAND
endmodule
