// Logisim project 1-AND_e_OR_2_Respostas.circ as structural Verilog: 1 circuit, main circuit main
module main (
  input  a,
  input  b,
  output a_b,
  output a_b_2
);

  and and_1 (a_b, a, b);
  or or_1 (a_b_2, a, b);
endmodule
