// Logisim project 2-AND_e_OR_1_Resposta_Selecionavel.circ as structural Verilog: 1 circuit, main circuit main
module main (
  input  a,
  input  b,
  input  chave,
  output a_OP_b
);

  wire and_out, or_out;

  and \and  (and_out, a, b);
  or \or  (or_out, a, b);
  Multiplexer #(.enable("false")) multiplexer_1 (.in0(and_out), .in1(or_out), .out(a_OP_b), .sel(chave));

  // Notes on the sheet:
  //   <OP> = Operação
  //   chave = 0  -->  <OP> = AND
  //   chave = 1  -->  <OP> = OR
endmodule
