// Logisim project 3-AND_OR_NAND_NOR_1_Resposta_Selecionavel.circ as structural Verilog: 1 circuit, main circuit main
module main (
  input  a,
  input  b,
  input  chave1_and_nand___or_nor,
  input  chave2_and_nand___or_nor,
  output a_OP_b
);

  wire and_out, multiplexer_1_out, multiplexer_2_out, nand_out, nor_out, or_out;

  and \and  (and_out, a, b);
  or \or  (or_out, a, b);
  nand \nand  (nand_out, a, b);
  nor \nor  (nor_out, a, b);
  Multiplexer #(.enable("false")) multiplexer_1 (
    .in0(and_out), .in1(or_out), .out(multiplexer_1_out), .sel(chave1_and_nand___or_nor));
  Multiplexer #(.enable("false")) multiplexer_2 (
    .in0(nand_out), .in1(nor_out), .out(multiplexer_2_out), .sel(chave1_and_nand___or_nor));
  Multiplexer #(.enable("false")) multiplexer_3 (
    .in0(multiplexer_1_out), .in1(multiplexer_2_out), .out(a_OP_b), .sel(chave2_and_nand___or_nor));

  // Notes on the sheet:
  //   <OP> = Operação
  //   chave1 = 0 e chave2 = 0  -->  <OP> = AND
  //   chave1 = 0 e chave2 = 1  -->  <OP> = NAND
  //   chave1 = 1 e chave2 = 0  -->  <OP> = OR
  //   chave1 = 1 e chave2 = 1  -->  <OP> = NOR
endmodule
