// Logisim project 4-OR_NOR_XOR_XNOR_1_Resposta_Selecionavel.circ as structural Verilog: 1 circuit, main circuit main
module main (
  input  a,
  input  b,
  input  [1:0] \chave_de_operações ,
  output a_OP_b
);

  wire nor_out, or_out, xnor_out, xor_out;

  or \or  (or_out, a, b);
  nor \nor  (nor_out, a, b);
  xor \xor  (xor_out, a, b);
  xnor \xnor  (xnor_out, a, b);
  Multiplexer #(.select(2), .enable("false")) multiplexer_1 (
    .in0(or_out), .in1(nor_out), .in2(xor_out), .in3(xnor_out), .out(a_OP_b), .sel(\chave_de_operações ));

  // Notes on the sheet:
  //   <OP> = Operação
  //   chave 00  -->  <OP> = OR
  //   chave 01  -->  <OP> = NOR
  //   chave 10  -->  <OP> = XOR
  //   chave 11  -->  <OP> = XNOR
endmodule
