// Logisim project 5-NOT_OR_NOR_AND_NAND_XOR_XNOR_1_Resposta_Selecionavel.circ as structural Verilog: 1 circuit, main circuit main
module main (
  input  a,
  input  b,
  input  [2:0] \chave_de_operações ,
  output a_OP_b
);

  wire and_out, nand_out, nor_out, not_a_out, or_out, xnor_out, xor_out;

  not not_a (not_a_out, a);
  or \or  (or_out, a, b);
  nor \nor  (nor_out, a, b);
  and \and  (and_out, a, b);
  nand \nand  (nand_out, a, b);
  xor \xor  (xor_out, a, b);
  xnor \xnor  (xnor_out, a, b);
  Multiplexer #(.select(3), .enable("false")) multiplexer_1 (
    .in0(not_a_out), .in1(or_out), .in2(nor_out), .in3(and_out), .in4(nand_out), .in5(xor_out),
    .in6(xnor_out), .out(a_OP_b), .sel(\chave_de_operações ));  // open: in7

  // Notes on the sheet:
  //   chave 001  -->  <OP> = OR
  //   chave 010  -->  <OP> = NOR
  //   chave 011  -->  <OP> = AND
  //   chave 101  -->  <OP> = XOR
  //   <OP> = Operação
  //   chave 000  -->  <OP> = NOT(a)
  //   chave 100  -->  <OP> = NAND
  //   chave 110  -->  <OP> = XNOR
endmodule
