// Logisim project 6-EQUALS_e_NOT_EQUALS_1_Resposta_Selecionavel.circ as structural Verilog: 1 circuit, main circuit main
module main (
  input  a,
  input  b,
  input  c,
  input  d,
  input  chave,
  output a_OP_b
);

  wire and_1_out, and_2_out, and_3_out, and_4_out, not_1_out, not_2_out, not_3_out, not_4_out, not_5_out,
       or_1_out;

  not not_1 (not_1_out, b);
  not not_2 (not_2_out, a);
  not not_3 (not_3_out, d);
  not not_4 (not_4_out, c);
  and and_1 (and_1_out, not_2_out, not_1_out, not_4_out, not_3_out);
  and and_2 (and_2_out, not_2_out, b, not_4_out, d);
  and and_3 (and_3_out, a, b, c, d);
  and and_4 (and_4_out, a, not_1_out, c, not_3_out);
  or or_1 (or_1_out, and_1_out, and_2_out, and_3_out, and_4_out);
  Multiplexer #(.enable("false")) multiplexer_1 (.in0(or_1_out), .in1(not_5_out), .out(a_OP_b), .sel(chave));
  not not_5 (not_5_out, or_1_out);

  // Notes on the sheet:
  //   ab.equals(cd) = a'.b'.c'.d' + a'.b.c.d' + a.b.c.d + a.b'.c.d'
  //   (EQUALS / NOT_EQUALS)_CHECKER
  //   <OP> = Operação
  //   chave = 0  -->  <OP> = EQUALS
  //   chave = 1  -->  <OP> = NOT_EQUALS
endmodule
