// Logisim project 7-GREATER_e_SMALLER_1_Resposta_Selecionavel.circ as structural Verilog: 1 circuit, main circuit main
module main (
  input  a,
  input  b,
  input  c,
  input  d,
  input  chave,
  output a_OP_b
);

  wire and_1_out, and_2_out, and_3_out, and_4_out, EQUALS___NOT_EQUALS__CHECKER_a_op_b, not_1_out, not_2_out,
       not_3_out, or_1_out;

  not not_1 (not_1_out, c);
  not not_2 (not_2_out, d);
  and and_1 (and_1_out, b, not_1_out, not_2_out);
  and and_2 (and_2_out, a, b, not_2_out);
  and and_3 (and_3_out, a, not_1_out);
  or or_1 (or_1_out, and_1_out, and_2_out, and_3_out);
  not not_3 (not_3_out, or_1_out);
  _6_EQUALS_e_NOT_EQUALS_1_Resposta_Selecionavel_main EQUALS___NOT_EQUALS__CHECKER (
    .a(d), .b(c), .c(b), .d(a), .chave(1'b1), .a_OP_b(EQUALS___NOT_EQUALS__CHECKER_a_op_b));
  and and_4 (and_4_out, not_3_out, EQUALS___NOT_EQUALS__CHECKER_a_op_b);
  Multiplexer #(.enable("false")) multiplexer_1 (.in0(or_1_out), .in1(and_4_out), .out(a_OP_b), .sel(chave));

  // Notes on the sheet:
  //   ab.greaterThan(cd) = b.c'.d' + a.b.d' + a.c'
  //   (GREATER / SMALLER)_CHECKER
  //   chave = 0  -->  EQUALS
  //   chave = 1  -->  NOT_EQUALS
  //   NOT_EQUALS
  //   <OP> = Operação
  //   chave = 0  -->  <OP> = GREATER
  //   chave = 1  -->  <OP> = SMALLER
  //   GREATER / SMALLER
endmodule
