// Logisim project 1-Somador_completo_4bits.circ as structural Verilog: 1 circuit, main circuit main
module main (
  input  [3:0] number1,
  input  [3:0] number2,
  input  received,
  output send_bit,
  output [3:0] number1___number2
);

  wire full_adder_2_send_bit, full_adder_3_send_bit, full_adder_4_send_bit;

  Somador_completo_2bits_mais_bit_recebido_main full_adder (
    .a(number1[3]), .b(number2[3]), .received(full_adder_2_send_bit), .send_bit(send_bit),
    .bit0(number1___number2[3]));
  Somador_completo_2bits_mais_bit_recebido_main full_adder_2 (
    .a(number1[2]), .b(number2[2]), .received(full_adder_3_send_bit), .send_bit(full_adder_2_send_bit),
    .bit0(number1___number2[2]));
  Somador_completo_2bits_mais_bit_recebido_main full_adder_3 (
    .a(number1[1]), .b(number2[1]), .received(full_adder_4_send_bit), .send_bit(full_adder_3_send_bit),
    .bit0(number1___number2[1]));
  Somador_completo_2bits_mais_bit_recebido_main full_adder_4 (
    .a(number1[0]), .b(number2[0]), .received(received), .send_bit(full_adder_4_send_bit),
    .bit0(number1___number2[0]));
endmodule
