// Logisim project 2-Subtrador_completo_4bits.circ as structural Verilog: 1 circuit, main circuit main
module main (
  input  [3:0] number1,
  input  [3:0] number2,
  input  lent,
  output borrow,
  output [3:0] number1___number2
);

  wire full_subtracter_2_borrow, full_subtracter_3_borrow, full_subtracter_4_borrow;

  Subtrador_completo_2bits_menos_bit_emprestado_main full_subtracter (
    .a(number1[3]), .b(number2[3]), .lent(full_subtracter_2_borrow), .borrow(borrow),
    .bit0(number1___number2[3]));
  Subtrador_completo_2bits_menos_bit_emprestado_main full_subtracter_2 (
    .a(number1[2]), .b(number2[2]), .lent(full_subtracter_3_borrow), .borrow(full_subtracter_2_borrow),
    .bit0(number1___number2[2]));
  Subtrador_completo_2bits_menos_bit_emprestado_main full_subtracter_3 (
    .a(number1[1]), .b(number2[1]), .lent(full_subtracter_4_borrow), .borrow(full_subtracter_3_borrow),
    .bit0(number1___number2[1]));
  Subtrador_completo_2bits_menos_bit_emprestado_main full_subtracter_4 (
    .a(number1[0]), .b(number2[0]), .lent(lent), .borrow(full_subtracter_4_borrow),
    .bit0(number1___number2[0]));
endmodule
