// Logisim project 4-NOT_EQUALS_4bits.circ as structural Verilog: 1 circuit, main circuit main
module main (
  input  [3:0] number1,
  input  [3:0] number2,
  output number1____number2
);

  wire EQUALS___NOT_EQUALS__CHECKER_p7, main_1_p5;

  // EQUALS_e_NOT_EQUALS_1_Resposta_Selecionavel_main main_1: pin names not known; wires that end beside it: number2[1], number2[0], number1[1], number1[0], main_1_p5, 1'b1
  // EQUALS_e_NOT_EQUALS_1_Resposta_Selecionavel_main EQUALS___NOT_EQUALS__CHECKER: pin names not known; wires that end beside it: number1, number2, number2[3], number2[2], number1[3], number1[2], EQUALS___NOT_EQUALS__CHECKER_p7, 1'b1
  or or_1 (number1____number2, main_1_p5, EQUALS___NOT_EQUALS__CHECKER_p7);

  // Notes on the sheet:
  //   NOT_EQUALS CHECKER
endmodule
