// Logisim project 5-ComplementoDe2_4bits.circ as structural Verilog: 1 circuit, main circuit main
module main (
  input  [3:0] number,
  output [3:0] minus_number
);

  wire [3:0] compl__de_1_nnumber;

  ComplementoDe1_4bits_main compl__de_1 (.number(number), .nnumber(compl__de_1_nnumber));
  _1_Somador_completo_4bits_main somador_de_4bits (
    .number1(compl__de_1_nnumber), .number2(4'b0001), .received(1'b0), .number1___number2(minus_number));  // open: send_bit
endmodule
