// Logisim project 6-Addition_subtraction_equals_e_not_equals_com_somador_algebrico_4bits.circ as structural Verilog: 1 circuit, main circuit main
module main (
  input  [2:0] \chave_de_operações ,
  input  [3:0] number1,
  input  [3:0] number2,
  output [3:0] num1_OP_num2
);

  wire nor_1_out, not_1_out;
  wire [3:0] bit_extender_1_out, bit_extender_2_out, somador_algebrico_number1_____number2;

  Somador_Algebrico_4bits_main somador_algebrico (
    .number1(number1), .number2(number2), .somar_sub(\chave_de_operações [2]),
    .number1_____number2(somador_algebrico_number1_____number2));
  nor nor_1 (nor_1_out, somador_algebrico_number1_____number2[0], somador_algebrico_number1_____number2[1], somador_algebrico_number1_____number2[2], somador_algebrico_number1_____number2[3]);
  not not_1 (not_1_out, nor_1_out);
  assign bit_extender_1_out = {{3{nor_1_out}}, nor_1_out};  // Bit_Extender bit_extender_1
  assign bit_extender_2_out = {{3{not_1_out}}, not_1_out};  // Bit_Extender bit_extender_2
  Multiplexer #(.select(3), .width(4), .enable("false")) multiplexer_1 (
    .in0(somador_algebrico_number1_____number2), .in4(somador_algebrico_number1_____number2),
    .in5(bit_extender_1_out), .in6(bit_extender_2_out), .out(num1_OP_num2), .sel(\chave_de_operações ));  // open: in1, in2, in3, in7

  // Notes on the sheet:
  //   chave = 000  -->  <OP> = addition
  //   chave = 100  -->  <OP> = subtraction
  //   chave = 101  -->  <OP> = equality
  //   chave = 110  -->  <OP> = not_equality
endmodule
