// Logisim project 7-Equals_e_not_equals_com_somador_algebrico_4bits.circ as structural Verilog: 1 circuit, main circuit main
module main (
  input  [3:0] number1,
  input  [3:0] number2,
  input  equals_not_equals,
  output number1_______number2
);

  wire nor_1_out, not_1_out;
  wire [3:0] somador_algebrico_number1_____number2;

  Somador_Algebrico_4bits_main somador_algebrico (
    .number1(number1), .number2(number2), .somar_sub(1'b1),
    .number1_____number2(somador_algebrico_number1_____number2));
  nor nor_1 (nor_1_out, somador_algebrico_number1_____number2[0], somador_algebrico_number1_____number2[1], somador_algebrico_number1_____number2[2], somador_algebrico_number1_____number2[3]);
  Multiplexer #(.enable("false")) multiplexer_1 (
    .in0(nor_1_out), .in1(not_1_out), .out(number1_______number2), .sel(equals_not_equals));
  not not_1 (not_1_out, nor_1_out);
endmodule
