// Logisim project ComplementoDe1_4bits.circ as structural Verilog: 1 circuit, main circuit main
module main (
  input  [3:0] number,
  output [3:0] nnumber
);

  assign nnumber = ~number;  // NOT_Gate not_1, 4 bits wide
endmodule
