// Logisim project Meio_somador.circ as structural Verilog: 1 circuit, main circuit main
module main (
  input  a,
  input  b,
  output send_bit,
  output bit0
);

  and and_1 (send_bit, a, b);
  xor xor_1 (bit0, a, b);

  // Notes on the sheet:
  //   a + b = send_bit bit0
  //   0 + 0 = 0             0
  //   0 + 1 = 0             1
  //   1 + 0 = 0             1
  //   1 + 1 = 1             0
endmodule
