// Logisim project Meio_subtrador.circ as structural Verilog: 1 circuit, main circuit main
module main (
  input  a,
  input  b,
  output borrow,
  output bit0
);

  wire not_1_out;

  not not_1 (not_1_out, a);
  and and_1 (borrow, not_1_out, b);
  xor xor_1 (bit0, a, b);

  // Notes on the sheet:
  //   0 - 0 = 0                  0
  //   0 - 1 = 1                  1
  //   1 - 0 = 0                  1
  //   1 - 1 = 0                  0
  //   a - b = borrow?    bit0
  //   borrow? informa se essa
  //   subtração pegou emprestado
  //   algum bit da próxima casa
  //   binária
endmodule
