// Logisim project Somador_Algebrico_4bits.circ as structural Verilog: 1 circuit, main circuit main
module main (
  input  [3:0] number1,
  input  [3:0] number2,
  input  somar_sub,
  output [3:0] number1_____number2
);

  wire [3:0] main_1_nnumber, multiplexer_1_out;

  ComplementoDe1_4bits_main main_1 (.number(number2), .nnumber(main_1_nnumber));
  Multiplexer #(.width(4), .enable("false")) multiplexer_1 (
    .in0(number2), .in1(main_1_nnumber), .out(multiplexer_1_out), .sel(somar_sub));
  _1_Somador_completo_4bits_main main_2 (
    .number1(number1), .number2(multiplexer_1_out), .received(somar_sub),
    .number1___number2(number1_____number2));  // open: send_bit
endmodule
