// Logisim project Subtrador_completo_2bits_menos_bit_emprestado.circ as structural Verilog: 1 circuit, main circuit main
module main (
  input  a,
  input  b,
  input  lent,
  output borrow,
  output bit0
);

  wire half_subtracter_2_borrow, half_subtracter_bit0, half_subtracter_borrow;

  Meio_subtrador_main half_subtracter (.a(a), .b(b), .borrow(half_subtracter_borrow), .bit0(half_subtracter_bit0));
  Meio_subtrador_main half_subtracter_2 (
    .a(half_subtracter_bit0), .b(lent), .borrow(half_subtracter_2_borrow), .bit0(bit0));
  or or_1 (borrow, half_subtracter_borrow, half_subtracter_2_borrow);

  // Notes on the sheet:
  //   lent? informa se a subtração
  //   atual emprestou algum bit para
  //   a casa binária anterior
  //   a - b - lent?
  //   borrow? informa se a subtração
  //   atual pegou emprestado
  //   algum bit da próxima casa
  //   binária
endmodule
