// Logisim project Flip_Flop_D.circ as structural Verilog: 1 circuit, main circuit main
module main (
  input  preset,
  input  data,
  input  clock,
  input  clear,
  output last_saved_data,
  output nlast_saved_data
);

  wire not_1_out;

  not not_1 (not_1_out, data);
  Flip_Flop_SR_main main_1 (
    .set(data), .clock(clock), .reset(not_1_out), .preset(preset), .clear(clear),
    .last_saved_data(last_saved_data), .nlast_saved_data(nlast_saved_data));
endmodule
