// Logisim project Flip_Flop_JK.circ as structural Verilog: 1 circuit, main circuit main
module main (
  input  preset,
  input  clock,
  input  J,
  input  clear,
  input  K,
  output last_saved_data,
  output nlast_saved_data
);

  wire and_1_out, and_2_out, not_1_out, or_1_out;

  and and_1 (and_1_out, nlast_saved_data, J);
  not not_1 (not_1_out, K);
  and and_2 (and_2_out, not_1_out, last_saved_data);
  or or_1 (or_1_out, and_1_out, and_2_out);
  Flip_Flop_D_main main_1 (
    .data(or_1_out), .clock(clock), .preset(preset), .clear(clear), .last_saved_data(last_saved_data),
    .nlast_saved_data(nlast_saved_data));
endmodule
