// Logisim project Flip_Flop_SR.circ as structural Verilog: 1 circuit, main circuit main
module main (
  input  preset,
  input  set,
  input  clock,
  input  reset,
  input  clear,
  output last_saved_data,
  output nlast_saved_data
);

  wire nand_1_out, nand_2_out, not_1_out, not_2_out;

  not not_1 (not_1_out, preset);
  nand nand_1 (nand_1_out, clock, set);
  nand nand_2 (nand_2_out, clock, reset);
  not not_2 (not_2_out, clear);
  nand nand_3 (last_saved_data, nand_1_out, not_1_out, nlast_saved_data);
  nand nand_4 (nlast_saved_data, last_saved_data, not_2_out, nand_2_out);
endmodule
